# Fritzing sketch schéma électrique (saved by Fritzing 0.9.3b)

parts:
  Part1 = Arduino Mega 2560 (Rev3)
  J1 = Basic Servo  # not connected
  J2 = Basic Servo  # not connected
  J3 = Basic Servo  # not connected
  J4 = Basic Servo  # not connected
  J5 = Basic Servo  # not connected
  J6 = Basic Servo  # not connected
  J9 = Basic Servo  # not connected
  J10 = Basic Servo  # not connected
  J11 = Basic Servo [part_number=1A]
  J12 = Basic Servo  # not connected
  J13 = Basic Servo  # not connected
  J14 = Basic Servo  # not connected
  J15 = Basic Servo  # not connected
  J16 = Basic Servo  # not connected
  J17 = Basic Servo  # not connected
  J18 = Basic Servo  # not connected
  J19 = Basic Servo  # not connected
  J20 = Basic Servo  # not connected
  J7 = Basic Servo  # not connected
  J8 = Basic Servo  # not connected
  BAT1 = Battery Holders [package=battery-aa-kit]
  Part2 = ACS712 Low Current Sensor Board v12
  C1 = Electrolytic Capacitor [capacitance=1µF package="100 mil [THT, electrolytic]"]
  U1 = Mini-360 DC-DC Buck converter [package=THT]
  Fuse1 = Fuse with Handler [part_number=Htc-15m]

nets:
  N1: Part1.A0, Part2.VO
  5V: Part1.5V, Part2.5V
  D42: J11.pulse
  N2: BAT1.+, Fuse1.Connector1
  N3: BAT1.-, U1.IN-
  N4: Part2.IP+, C1.-, U1.OUT+
  N5: C1.+, U1.OUT-
  N6: U1.IN+, Fuse1.Connector2

notes:
  Batterie Makita 12 V 4000mAh
  12 V
  6.5V
  capteur de courant
  convertisseur dc-dc
  1A
  1B
  1C
  3A
  3B
  3C
  5A
  5B
  5C
  2A
  2B
  2C
  4A
  4B
  4C
  6A
  6B
  6C
  tete
  mandibule

custom parts:
  Mini-360 DC-DC Buck converter: Mini-360 DC-DC Buck converter. Tiny buck step down voltage converter, input voltage 4.75 to 23V output 1 to 17V adjustable. Available from ebay and the like.
